# Fritzing sketch Circuit (saved by Fritzing 0.9.3b)

parts:
  U1 = NodeMCU V1.0
  Mod1 = ESP32 - CAM
  Part1 = Bluetooth HC-05 Macho
  PWM1 = PCA9685 16x12-bit PWM Breakout
  Part3 = InvenSense MPU6050
  VCC2 = Battery block 9V
  IC1 = Voltage Regulator [package=to-220-alt]
  U2 = NodeMCU V1.0
  Part5 = InvenSense MPU6050
  IC2 = Voltage Regulator [package=to-220-alt]
  VCC3 = Battery block 9V

nets:
  N1: U1.D1, Part3.SCL
  N2: U1.D2, Part3.SDA
  GND: U1.GND, Part1.GND, Part3.GND
  N3: U1.D7, Part1.TXD
  N4: U1.D8, Part1.RXD
  N5: U1.Vin, IC1.OUT
  N6: Mod1.5V, PWM1.no_name_yet#505
  N7: Mod1.GND, PWM1.no_name_yet#501
  N8: Mod1.IO15, PWM1.no_name_yet#503
  N9: Mod1.IO14, PWM1.no_name_yet#504
  N10: VCC2.-, IC1.IN
  N11: VCC2.+, IC1.GND
  N12: U2.D1, Part5.SCL
  N13: U2.D2, Part5.SDA
  GND_2: U2.GND, Part5.GND
  N14: U2.Vin, IC2.OUT
  N15: IC2.GND, VCC3.+
  N16: IC2.IN, VCC3.-

notes:
  Left hand
  Right hand
  Master hand
  Slave hand
  Servo outputs

custom parts:
  NodeMCU V1.0: ESP8266 based NodeMCU
  ESP32 - CAM: The ESP32-CAM has a very competitive small-size camera module that can operate independently as a minimum system with a footprint of only 27*40.5*4.5mm and a deep sleep current of up to 6mA.
